# Fritzing sketch mqtt_send_digital (saved by Fritzing 0.9.2b)
breadboards: 1

parts:
  LED1 = LED - 5mm [color="Red (633nm)" package="5 mm [THT]"]
  S1 = Pushbutton [package="[THT]"]
  R1 = Resistor [tolerance=±5% resistance=220 package=THT]
  Part4 = Arduino Ethernet Shield (Rev3)

nets:
  N1: LED1.cathode, S1.Pin_3, S1.Pin_4, Part4.GND
  N2: LED1.anode, R1.Pin_0
  N3: S1.Pin_1, S1.Pin_2, Part4.D2
  N4: R1.Pin_1, Part4.SPI/D13

custom parts:
  Arduino Ethernet Shield (Rev3): The Arduino Ethernet Shield allows an Arduino board to connect to the internet. It is based on the Wiznet W5100 ethernet chip (datasheet). The Wiznet W5100 provides a network (IP) stack capable of both TCP and UDP. It supports up to four simultaneous socket connections. Use the Ethernet library to write sketches which connect to the internet using the shield. The ethernet shield connects to an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
